// Logisim project SAP1.circ as structural Verilog: 1 circuit, main circuit main
module main (
);

  wire and_1_out, Carry, Clk, clock_1_out, decoder_1_out3, decoder_1_out4, decoder_1_out5, decoder_2_out0,
       decoder_2_out1, decoder_2_out2, decoder_2_out3, decoder_2_out6, decoder_2_out7, decoder_2_out11,
       decoder_2_out15, decoder_2_out18, decoder_2_out19, decoder_2_out21, decoder_2_out22, decoder_2_out23,
       decoder_2_out25, decoder_2_out26, decoder_2_out27, decoder_2_out29, decoder_2_out30, decoder_2_out31,
       decoder_2_out33, decoder_2_out34, decoder_2_out35, decoder_2_out36, decoder_2_out37, decoder_2_out38,
       decoder_2_out39, decoder_2_out40, decoder_2_out41, decoder_2_out42, decoder_2_out43, decoder_2_out44,
       decoder_2_out45, decoder_2_out46, decoder_2_out47, decoder_2_out48, decoder_2_out49, decoder_2_out50,
       decoder_2_out51, decoder_2_out52, decoder_2_out53, decoder_2_out54, decoder_2_out55, decoder_2_out57,
       decoder_2_out58, decoder_2_out59, decoder_2_out61, decoder_2_out62, decoder_2_out63, EN_A, EN_A1,
       EN_A2, EN_A3, EN_A4, EN_F, EN_Ram, Halt, IO, IO1, IO2, IO3, IO4, IO6, IO7, IO8, LD, LD1, LD2, LI, Lm,
       Lm0, Lo, Load, Load2, Load3, NClk, or_2_out, or_3_out, Out_A, Out_B, PCInc, Reset, RO, ZF;
  wire [1:0] priority_encoder_1_out;
  wire [1:1] priority_encoder_1_en_out;
  wire [2:0] counter_1_q;
  wire [3:0] controlled_buffer_1_out, controlled_buffer_1_out_2, Instruction_Reg_q, MAR_q, Output_Reg_q,
       Output_Reg_q_2, Program_Counter_q;
  wire [5:0] or_4_out;
  wire [7:0] adder_1_out, FI_R, ram_1_dout, REG_A_q, REG_B_q, xor_1_out;

  Clock clock_1 (.out(clock_1_out));
  RAM #(.addrWidth(4)) ram_1 (
    .addr(MAR_q), .oe(1'b1), .clk(NClk), .din({controlled_buffer_1_out_2, controlled_buffer_1_out}),
    .dout(ram_1_dout));  // open: we
  Button button_1 (.out(Reset));
  or or_1 (Clk, Halt, clock_1_out);
  Counter #(.max('hf), .width(4)) Program_Counter (
    .clr(Reset), .load(Load), .up(1'b1), .clk(or_2_out), .D(controlled_buffer_1_out), .Q(Program_Counter_q));  // open: count, carry
  or or_2 (or_2_out, Load, PCInc);
  Register Instruction_Reg (
    .D({controlled_buffer_1_out_2, controlled_buffer_1_out}), .en(LI), .clk(Clk),
    .Q({or_4_out[5:2], Instruction_Reg_q}), .clr(Reset));
  or or_3 (or_3_out, and_1_out, Reset);
  Counter #(.max('h7), .width(3)) counter_1 (
    .clr(or_3_out), .load(1'b0), .up(1'b1), .count(1'b1), .clk(NClk), .Q(counter_1_q));  // open: D, carry
  Register #(.width(4)) MAR (.D(controlled_buffer_1_out), .en(Lm), .clk(Clk), .Q(MAR_q), .clr(Reset));
  not not_1 (NClk, Clk);
  and and_1 (and_1_out, counter_1_q[2], counter_1_q[1]);  // AND_Gate
  assign {controlled_buffer_1_out_2, controlled_buffer_1_out} = RO ? ram_1_dout : 8'bz;  // Controlled_Buffer controlled_buffer_1
  assign {controlled_buffer_1_out_2, controlled_buffer_1_out} = IO ? {4'b0000, Instruction_Reg_q} : 8'bz;  // Controlled_Buffer controlled_buffer_2
  Decoder #(.select(3)) decoder_1 (
    .out0(Lm0), .out1(PCInc), .out2(LI), .out3(decoder_1_out3), .out4(decoder_1_out4), .out5(decoder_1_out5),
    .sel(counter_1_q));  // open: out6, out7, en
  assign {controlled_buffer_1_out_2, controlled_buffer_1_out} = Lm0 ? {4'b0000, Program_Counter_q} : 8'bz;  // Controlled_Buffer controlled_buffer_3
  assign {controlled_buffer_1_out_2, controlled_buffer_1_out} = Out_A ? REG_A_q : 8'bz;  // Controlled_Buffer controlled_buffer_4
  assign {controlled_buffer_1_out_2, controlled_buffer_1_out} = Out_B ? REG_B_q : 8'bz;  // Controlled_Buffer controlled_buffer_5
  assign {controlled_buffer_1_out_2, controlled_buffer_1_out} = EN_A2 ? adder_1_out : 8'bz;  // Controlled_Buffer controlled_buffer_6
  Priority_Encoder #(.select(2)) priority_encoder_1 (
    .in0(decoder_1_out3), .in1(decoder_1_out4), .in2(decoder_1_out5), .in3(1'b0),
    .out(priority_encoder_1_out), .en_out(priority_encoder_1_en_out[1]));  // open: gs, en_in
  assign or_4_out[1:0] = priority_encoder_1_out | {2{priority_encoder_1_en_out[1]}};  // OR_Gate or_4, 2 bits wide
  Register REG_A (
    .D({controlled_buffer_1_out_2, controlled_buffer_1_out}), .en(EN_A), .clk(Clk), .Q(REG_A_q), .clr(Reset));
  Adder adder_1 (.a(REG_A_q), .b(xor_1_out), .out(adder_1_out), .cout(Carry));  // open: cin
  assign xor_1_out = {8{EN_A3}} ^ REG_B_q;  // XOR_Gate xor_1, 8 bits wide
  Register REG_B (
    .D({controlled_buffer_1_out_2, controlled_buffer_1_out}), .en(LD), .clk(Clk), .Q(REG_B_q), .clr(Reset));
  Register Output_Reg (
    .D({controlled_buffer_1_out_2, controlled_buffer_1_out}), .en(Lo), .clk(Clk),
    .Q({Output_Reg_q_2, Output_Reg_q}), .clr(Reset));
  Hex_Digit_Display hex_digit_display_1 (.value(Output_Reg_q_2));  // open: dp
  Decoder #(.enable("false"), .select(6)) decoder_2 (
    .out0(decoder_2_out0), .out1(decoder_2_out1), .out2(decoder_2_out2), .out3(decoder_2_out3), .out4(IO1),
    .out5(EN_A1), .out6(decoder_2_out6), .out7(decoder_2_out7), .out8(IO2), .out9(LD1), .out10(EN_A2),
    .out11(decoder_2_out11), .out12(IO3), .out13(LD2), .out14(EN_A3), .out15(decoder_2_out15), .out16(IO4),
    .out17(EN_Ram), .out18(decoder_2_out18), .out19(decoder_2_out19), .out20(EN_A4), .out21(decoder_2_out21),
    .out22(decoder_2_out22), .out23(decoder_2_out23), .out24(IO6), .out25(decoder_2_out25),
    .out26(decoder_2_out26), .out27(decoder_2_out27), .out28(IO7), .out29(decoder_2_out29),
    .out30(decoder_2_out30), .out31(decoder_2_out31), .out32(IO8), .out33(decoder_2_out33),
    .out34(decoder_2_out34), .out35(decoder_2_out35), .out36(decoder_2_out36), .out37(decoder_2_out37),
    .out38(decoder_2_out38), .out39(decoder_2_out39), .out40(decoder_2_out40), .out41(decoder_2_out41),
    .out42(decoder_2_out42), .out43(decoder_2_out43), .out44(decoder_2_out44), .out45(decoder_2_out45),
    .out46(decoder_2_out46), .out47(decoder_2_out47), .out48(decoder_2_out48), .out49(decoder_2_out49),
    .out50(decoder_2_out50), .out51(decoder_2_out51), .out52(decoder_2_out52), .out53(decoder_2_out53),
    .out54(decoder_2_out54), .out55(decoder_2_out55), .out56(Lo), .out57(decoder_2_out57),
    .out58(decoder_2_out58), .out59(decoder_2_out59), .out60(Halt), .out61(decoder_2_out61),
    .out62(decoder_2_out62), .out63(decoder_2_out63), .sel(or_4_out));
  Register register_1 (.D({{6{1'b0}}, Carry, ZF}), .en(EN_F), .clk(Clk), .Q(FI_R), .clr(Reset));
  Hex_Digit_Display hex_digit_display_2 (.value(Output_Reg_q));  // open: dp
  nor nor_1 (ZF, adder_1_out[7], adder_1_out[6], adder_1_out[5], adder_1_out[4], adder_1_out[3], adder_1_out[2], adder_1_out[1], adder_1_out[0]);
  LedBar ledbar_1 (
    .led0(Output_Reg_q_2[3]), .led1(Output_Reg_q_2[2]), .led2(Output_Reg_q_2[1]), .led3(Output_Reg_q_2[0]),
    .led4(Output_Reg_q[3]), .led5(Output_Reg_q[2]), .led6(Output_Reg_q[1]), .led7(Output_Reg_q[0]));
  and and_2 (Load2, FI_R[1], IO7);
  and and_3 (Load3, FI_R[0], IO8);
  or or_5 (Out_A, EN_Ram, Lo);
  or or_6 (LD, LD1, LD2);
  or or_7 (EN_F, EN_A2, EN_A3);
  or or_8 (Load, IO6, Load3, Load2);
  or or_9 (IO, IO8, IO7, IO6, IO4, IO3, EN_A4, IO2, IO1);
  or or_10 (Lm, IO2, IO4, Lm0, IO3, IO1);
  or or_11 (RO, LD1, LI, EN_A1, LD2);
  or or_12 (EN_A, EN_A3, EN_A1, EN_A2, EN_A4);

  // Other names for the same wires on the sheet: EN_F2 = EN_A3; SF = EN_A3; IO5 = EN_A4; Lm1 = IO1; Lm2 = IO2;
  //   Lm3 = IO3; Lm4 = IO4; Load1 = IO6; Out_A1 = EN_Ram; Out_A2 = Lo; EN_F1 = EN_A2; Out_ALU = EN_A2; PO = Lm0;
  //   RO1 = LI; RO2 = EN_A1; RO3 = LD1; RO4 = LD2
endmodule
